# Fritzing sketch music_instrument (saved by Fritzing 0.9.3b)
circuit board: 8.46667cm x 5.64444cm
breadboards: 1

parts:
  Part1 = Arduino Uno (Rev3)
  LED1 = LED - 5mm [color="Red (633nm)" package="5 mm [THT]"]
  LED2 = LED - 5mm [color="Red (633nm)" package="5 mm [THT]"]
  R1 = Resistor [tolerance=±5% resistance=220 package=THT]
  hc-sr1 = hc-sr04
  J1 = Piezo Speaker

nets:
  N1: Part1.D8, hc-sr1.Echo
  N2: Part1.D12/MISO, R1.Pin_0
  GND: Part1.GND, hc-sr1.GND, J1.pin2
  N3: Part1.D2, LED1.anode
  N4: Part1.D4, LED2.anode
  N5: Part1.D7, hc-sr1.Trig
  5V: Part1.5V, hc-sr1.VCC
  N6: R1.Pin_1, J1.pin1
